// Logisim project cpu.circ as structural Verilog: 7 circuits, main circuit main
module main (
);

  wire CLK, i_PC, i_R0, i_R1, i_RAM, jump_check_1_jump, R, X, ZR0, ZR1;
  wire [2:0] alu_s_1_s, I;
  wire [5:0] incr_6bit_1_i_incr, multiplexer_1_out, PC_q;
  wire [7:0] alu_i_1_a, alu_i_1_b, AO, QR0, QR1, QRAM, V;
  wire [15:13] rom_1_data;

  Clock clock_1 (.out(CLK));
  incr_6bit incr_6bit_1 (.i(PC_q), .i_incr(incr_6bit_1_i_incr));
  jump_check jump_check_1 (.ZR0(ZR0), .ZR1(ZR1), .R(R), .I(I), .JUMP(jump_check_1_jump));
  alu_o alu_o_1 (.R(R), .I(I), .i_RAM(i_RAM), .i_R0(i_R0), .i_R1(i_R1), .i_PC(i_PC));
  Register R0 (.D(AO), .en(i_R0), .clk(CLK), .Q(QR0));  // open: clr
  Register R1 (.D(AO), .en(i_R1), .clk(CLK), .Q(QR1));  // open: clr
  Multiplexer #(.width(6)) multiplexer_1 (
    .in0(incr_6bit_1_i_incr), .in1(AO[6:1]), .out(multiplexer_1_out), .sel(jump_check_1_jump));
  alu_i alu_i_1 (.I(I), .X(X), .R(R), .R0(QR0), .R1(QR1), .V(V), .RAM(QRAM), .A(alu_i_1_a), .B(alu_i_1_b));
  alu_s alu_s_1 (.I(I), .S(alu_s_1_s));
  Register #(.width(6)) PC (.D(multiplexer_1_out), .en(CLK), .clk(CLK), .Q(PC_q));  // open: clr
  nor nor_1 (ZR0, QR0[3], QR0[0], QR0[1], QR0[2], QR0[4], QR0[5], QR0[6], QR0[7]);
  nor nor_2 (ZR1, QR1[3], QR1[0], QR1[1], QR1[2], QR1[4], QR1[5], QR1[6], QR1[7]);
  ROM #(.addrWidth(6), .dataWidth(16)) rom_1 (.addr(PC_q), .data({rom_1_data, I, X, R, V}));
  ALU alu_1 (.A(alu_i_1_a), .B(alu_i_1_b), .S(alu_s_1_s), .AO(AO));
  RAM #(.addrWidth(7)) ram_1 (.addr(V[6:0]), .we(i_RAM), .oe(1'b1), .clk(CLK), .din(AO), .dout(QRAM));

  // Notes on the sheet:
  //   contents of rom_1 (hex, n*v repeats v):
  //   0 11a 580 28a 1200 481
endmodule

module ALU (
  input  [7:0] A,
  input  [7:0] B,
  input  [2:0] S,
  output [7:0] AO
);

  wire [7:0] adder_1_out, and_1_out, multiplexer_1_out, not_1_out, or_1_out;

  assign not_1_out = ~B;  // NOT_Gate not_1, 8 bits wide
  Multiplexer #(.width(8)) multiplexer_1 (.in0(B), .in1(not_1_out), .out(multiplexer_1_out), .sel(S[2]));
  assign and_1_out = A & B;  // AND_Gate and_1, 8 bits wide
  assign or_1_out = A | B;  // OR_Gate or_1, 8 bits wide
  Adder adder_1 (.a(A), .b(multiplexer_1_out), .out(adder_1_out), .cin(S[2]));  // open: cout
  Multiplexer #(.select(2), .width(8)) multiplexer_2 (
    .in0(adder_1_out), .in1(and_1_out), .in2(or_1_out), .in3(A), .out(AO), .sel(S[1:0]));
endmodule

module alu_s (
  input  [2:0] I,
  output [2:0] S
);

  wire and_1_out, and_2_out;

  and and_1 (and_1_out, ~I[0], I[1]);  // AND_Gate
  and and_2 (and_2_out, I[0], I[1]);
  and and_3 (S[2], I[0], ~I[1], I[2]);  // AND_Gate
  or or_1 (S[0], and_1_out, ~I[2]);  // OR_Gate
  or or_2 (S[1], and_2_out, ~I[2]);  // OR_Gate
endmodule

module alu_o (
  input  R,
  input  [2:0] I,
  output i_RAM,
  output i_R0,
  output i_R1,
  output i_PC
);

  wire nor_1_out, not_1_out, or_1_out;

  not not_1 (not_1_out, R);
  nor nor_1 (nor_1_out, I[0], I[1]);
  or or_1 (or_1_out, nor_1_out, I[2]);
  and and_1 (i_PC, I[1], ~I[2]);  // AND_Gate
  and and_2 (i_RAM, I[0], ~I[1], ~I[2]);  // AND_Gate
  and and_3 (i_R0, not_1_out, or_1_out);
  and and_4 (i_R1, R, or_1_out);
endmodule

module jump_check (
  input  ZR0,
  input  ZR1,
  input  R,
  input  [2:0] I,
  output JUMP
);

  wire and_1_out, and_2_out, and_3_out, and_4_out, not_1_out;

  not not_1 (not_1_out, R);
  and and_1 (and_1_out, I[0], I[1], ~I[2]);  // AND_Gate
  and and_2 (and_2_out, ~I[0], I[1], ~I[2]);  // AND_Gate
  and and_3 (and_3_out, ZR0, not_1_out, and_1_out);
  and and_4 (and_4_out, ZR1, R, and_1_out);
  or or_1 (JUMP, and_3_out, and_4_out, and_2_out);
endmodule

module alu_i (
  input  [2:0] I,
  input  X,
  input  R,
  input  [7:0] R0,
  input  [7:0] R1,
  input  [7:0] V,
  input  [7:0] RAM,
  output [7:0] A,
  output [7:0] B
);

  wire and_1_out, and_2_out, and_3_out, and_4_out, and_5_out, and_6_out, or_3_out;
  wire [1:0] and_7_out, or_2_out;

  and and_1 (and_1_out, ~I[2], ~I[1], ~I[0]);  // AND_Gate
  and and_2 (and_2_out, ~I[2], I[1]);  // AND_Gate
  and and_3 (and_3_out, I[2], ~X, R);  // AND_Gate
  or or_1 (or_2_out[1], and_1_out, and_2_out);
  and and_4 (and_4_out, I[2], ~I[1], I[0], R);  // AND_Gate
  or or_2 (or_2_out[0], and_3_out, and_4_out, and_5_out, and_6_out);
  and and_5 (and_5_out, ~I[2], ~I[1], I[0], R);  // AND_Gate
  and and_6 (and_6_out, ~I[2], ~I[1], ~I[0], X);  // AND_Gate
  Multiplexer #(.select(2), .width(8)) multiplexer_1 (.in0(R0), .in1(R1), .in2(V), .in3(RAM), .out(A), .sel(or_2_out));
  not not_1 (and_7_out[1], X);
  and and_7 (and_7_out[0], X, or_3_out);
  Multiplexer #(.select(2), .width(8)) multiplexer_2 (.in0(R0), .in1(R1), .in2(V), .in3(RAM), .out(B), .sel(and_7_out));
  or or_3 (or_3_out, I[1], ~R, ~I[0]);  // OR_Gate
endmodule

module incr_6bit (
  input  [5:0] i,
  output [5:0] i_incr
);

  wire and_1_out, and_2_out, and_3_out, and_4_out, and_5_out;

  and and_1 (and_1_out, i[0], 1'b1);
  xor xor_1 (i_incr[0], 1'b1, i[0]);
  xor xor_2 (i_incr[1], and_1_out, i[1]);
  and and_2 (and_2_out, and_1_out, i[1]);
  xor xor_3 (i_incr[2], and_2_out, i[2]);
  and and_3 (and_3_out, and_2_out, i[2]);
  xor xor_4 (i_incr[3], and_3_out, i[3]);
  and and_4 (and_4_out, and_3_out, i[3]);
  xor xor_5 (i_incr[4], and_4_out, i[4]);
  and and_5 (and_5_out, and_4_out, i[4]);
  xor xor_6 (i_incr[5], and_5_out, i[5]);
  // AND_Gate and_6 has open pins: in0=and_5_out, in1=i[5], out=open
endmodule
